# Fritzing sketch Fritz_kissingBreathTest (saved by Fritzing 0.9.2b)
breadboards: 1

parts:
  Part1 = Arduino Uno (Rev3)
  R1 = Resistor [tolerance=±5% resistance=220 package="2512 [SMD]"]
  R2 = Resistor [tolerance=±5% resistance=220 package="2512 [SMD]"]
  R3 = Resistor [tolerance=±5% resistance=220 package="2512 [SMD]"]
  R4 = Resistor [tolerance=±5% resistance=220 package="2512 [SMD]"]
  LED1 = smd LED [color="Red (633nm)" package="0805 [SMD]"]
  LED2 = smd LED [color="Red (633nm)" package="0805 [SMD]"]
  LED3 = smd LED [color="Red (633nm)" package="0805 [SMD]"]
  LED4 = smd LED [color="Red (633nm)" package="0805 [SMD]"]
  LED5 = smd LED [color="Red (633nm)" package="0805 [SMD]"]
  LED6 = smd LED [color="Red (633nm)" package="0805 [SMD]"]
  R5 = Resistor [tolerance=±5% resistance=220 package="2512 [SMD]"]
  R6 = Resistor [tolerance=±5% resistance=220 package="2512 [SMD]"]

nets:
  N1: Part1.GND, LED1.cathode, LED2.cathode, LED3.cathode, LED4.cathode, LED5.cathode, LED6.cathode
  N2: Part1.D2, R6.Pin_1
  N3: Part1.D3_PWM, R5.Pin_1
  N4: Part1.D4, R3.Pin_1
  N5: Part1.D5_PWM, R2.Pin_1
  N6: Part1.D6_PWM, R1.Pin_1
  N7: Part1.D7, R4.Pin_1
  N8: R1.Pin_0, LED2.anode
  N9: R2.Pin_0, LED3.anode
  N10: R3.Pin_0, LED4.anode
  N11: R4.Pin_0, LED1.anode
  N12: LED5.anode, R5.Pin_0
  N13: LED6.anode, R6.Pin_0
